// Logisim project bcdto7.circ as structural Verilog: 10 circuits, main circuit main
module main (
);

  wire n7_segment_0_9_reverse_1_out_1, n7_segment_0_9_reverse_1_out_2, n7_segment_0_9_reverse_1_out_3,
       n7_segment_0_9_reverse_1_out_4, n7_segment_0_9_reverse_2_out_5, n7_segment_0_9_reverse_2_out_6,
       n7_segment_0_9_reverse_2_out_7;

  _7_segment_0_9_reverse u_7_segment_0_9_reverse_1 (
    .out_1(n7_segment_0_9_reverse_1_out_1), .out_2(n7_segment_0_9_reverse_1_out_2),
    .out_3(n7_segment_0_9_reverse_1_out_3), .out_4(n7_segment_0_9_reverse_1_out_4));  // open: out_5, out_6, out_7
  _7_Segment_Display u_7_segment_display_1 (
    .g(n7_segment_0_9_reverse_1_out_1), .f(n7_segment_0_9_reverse_1_out_2),
    .a(n7_segment_0_9_reverse_1_out_3), .b(n7_segment_0_9_reverse_1_out_4),
    .e(n7_segment_0_9_reverse_2_out_5), .d(n7_segment_0_9_reverse_2_out_6), .c(n7_segment_0_9_reverse_2_out_7));  // open: dp
  _7_segment_0_9_reverse u_7_segment_0_9_reverse_2 (
    .out_5(n7_segment_0_9_reverse_2_out_5), .out_6(n7_segment_0_9_reverse_2_out_6),
    .out_7(n7_segment_0_9_reverse_2_out_7));  // open: out_1, out_2, out_3, out_4
endmodule

module a09 (
  input  A,
  input  B,
  input  C,
  input  D,
  output a_2
);

  wire not_1_out, xor_1_out;

  xor xor_1 (xor_1_out, B, D);
  not not_1 (not_1_out, xor_1_out);
  or or_1 (a_2, A, C, not_1_out);

  // Notes on the sheet:
  //   a= A + C + BxnorD
endmodule

module b09 (
  input  A,
  input  B,
  input  C,
  input  D,
  output b_2
);

  wire not_1_out, xnor_1_out;

  not not_1 (not_1_out, B);
  xnor xnor_1 (xnor_1_out, C, D);
  or or_1 (b_2, not_1_out, xnor_1_out);

  // Notes on the sheet:
  //   b=B' + CxnorD
endmodule

module c09 (
  input  A,
  input  B,
  input  C,
  input  D,
  output c_2
);

  wire not_1_out;

  not not_1 (not_1_out, C);
  or or_1 (c_2, B, not_1_out, D);

  // Notes on the sheet:
  //   c= B + C' + D
endmodule

module d09 (
  input  A,
  input  B,
  input  C,
  input  D,
  output d_2
);

  wire and_1_out, and_2_out, and_3_out, and_4_out, not_1_out, not_2_out, not_3_out;

  not not_1 (not_1_out, B);
  not not_2 (not_2_out, D);
  not not_3 (not_3_out, C);
  and and_1 (and_1_out, not_2_out, C);
  and and_2 (and_2_out, not_1_out, C);
  and and_3 (and_3_out, not_1_out, not_2_out);
  and and_4 (and_4_out, B, not_3_out, D);
  or or_1 (d_2, A, and_2_out, and_3_out, and_1_out, and_4_out);

  // Notes on the sheet:
  //   2107096
endmodule

module e09 (
  input  A,
  input  B,
  input  C,
  input  D,
  output e
);

  wire and_1_out, and_2_out, not_1_out, not_2_out;

  not not_1 (not_1_out, B);
  not not_2 (not_2_out, D);
  and and_1 (and_1_out, not_1_out, not_2_out);
  and and_2 (and_2_out, C, not_2_out);
  or or_1 (e, and_1_out, and_2_out);
endmodule

// f
module f09 (
  input  A,
  input  B,
  input  C,
  input  D,
  output f
);

  wire and_1_out, and_2_out, and_3_out, not_1_out, not_2_out;

  not not_1 (not_1_out, C);
  not not_2 (not_2_out, D);
  and and_1 (and_1_out, B, not_1_out);
  and and_2 (and_2_out, B, not_2_out);
  and and_3 (and_3_out, not_1_out, not_2_out);
  or or_1 (f, A, and_1_out, and_2_out, and_3_out);
endmodule

module g09 (
  input  A,
  input  B,
  input  C,
  input  D,
  output g
);

  wire and_1_out, not_1_out, xor_1_out;

  not not_1 (not_1_out, D);
  xor xor_1 (xor_1_out, B, C);
  and and_1 (and_1_out, C, not_1_out);
  or or_1 (g, A, xor_1_out, and_1_out);

  // Notes on the sheet:
  //   g=A + CD' + BxorC
endmodule

module _4_bit_sync_down_counter__9_0 (
  output out_1,
  output out_2,
  output out_3,
  output out_4
);

  wire _0_qn, _1_qn, _2_qn, _3_qn, and_1_out, and_2_out, and_3_out, and_4_out, and_5_out, and_6_out,
       and_7_out, and_8_out, clock_1_out, or_1_out, or_2_out, or_3_out;

  or or_1 (or_1_out, and_1_out, and_2_out, and_3_out);
  or or_2 (or_2_out, and_4_out, and_5_out, and_6_out);
  or or_3 (or_3_out, and_7_out, and_8_out);
  Clock clock_1 (.out(clock_1_out));
  and and_1 (and_1_out, _0_qn, _1_qn, out_2);
  and and_2 (and_2_out, _0_qn, out_1);
  and and_3 (and_3_out, out_4, out_3);
  and and_4 (and_4_out, _0_qn, out_1);
  and and_5 (and_5_out, out_3, out_2);
  and and_6 (and_6_out, out_4, out_2);
  and and_7 (and_7_out, out_1, out_4);
  and and_8 (and_8_out, _3_qn, _2_qn, _1_qn, _0_qn);
  D_Flip_Flop _0 (.clk(clock_1_out), .D(_0_qn), .Q(out_4), .Qn(_0_qn));  // open: preset, en, reset
  D_Flip_Flop _1 (.clk(clock_1_out), .D(or_1_out), .Q(out_3), .Qn(_1_qn));  // open: preset, en, reset
  D_Flip_Flop _2 (.clk(clock_1_out), .D(or_2_out), .Q(out_2), .Qn(_2_qn));  // open: preset, en, reset
  D_Flip_Flop _3 (.clk(clock_1_out), .D(or_3_out), .Q(out_1), .Qn(_3_qn));  // open: preset, en, reset

  // Notes on the sheet:
  //   2107096
  //                                         D1 = Q1Q0 + Q3Q0' + Q2Q1'
  //                                                       D2 = Q2Q0 + Q2Q1 + Q3Q0'
  //   D3 = Q3Q0 + Q3'Q2'Q1'Q0'
  //                D0 = Q0'
endmodule

module _7_segment_0_9_reverse (
  output out_1,
  output out_2,
  output out_3,
  output out_4,
  output out_5,
  output out_6,
  output out_7
);

  wire n4_bit_sync_down_counter_9_0_1_out_1, n4_bit_sync_down_counter_9_0_1_out_2,
       n4_bit_sync_down_counter_9_0_1_out_3, n4_bit_sync_down_counter_9_0_1_out_4;

  _4_bit_sync_down_counter__9_0 u_4_bit_sync_down_counter_9_0_1 (
    .out_1(n4_bit_sync_down_counter_9_0_1_out_1), .out_2(n4_bit_sync_down_counter_9_0_1_out_2),
    .out_3(n4_bit_sync_down_counter_9_0_1_out_3), .out_4(n4_bit_sync_down_counter_9_0_1_out_4));
  a09 a09_1 (
    .A(n4_bit_sync_down_counter_9_0_1_out_1), .B(n4_bit_sync_down_counter_9_0_1_out_2),
    .C(n4_bit_sync_down_counter_9_0_1_out_3), .D(n4_bit_sync_down_counter_9_0_1_out_4), .a_2(out_3));
  b09 b09_1 (
    .A(n4_bit_sync_down_counter_9_0_1_out_1), .B(n4_bit_sync_down_counter_9_0_1_out_2),
    .C(n4_bit_sync_down_counter_9_0_1_out_3), .D(n4_bit_sync_down_counter_9_0_1_out_4), .b_2(out_4));
  f09 f09_1 (
    .A(n4_bit_sync_down_counter_9_0_1_out_1), .B(n4_bit_sync_down_counter_9_0_1_out_2),
    .C(n4_bit_sync_down_counter_9_0_1_out_3), .D(n4_bit_sync_down_counter_9_0_1_out_4), .f(out_2));
  g09 g09_1 (
    .A(n4_bit_sync_down_counter_9_0_1_out_1), .B(n4_bit_sync_down_counter_9_0_1_out_2),
    .C(n4_bit_sync_down_counter_9_0_1_out_3), .D(n4_bit_sync_down_counter_9_0_1_out_4), .g(out_1));
  c09 c09_1 (
    .A(n4_bit_sync_down_counter_9_0_1_out_1), .B(n4_bit_sync_down_counter_9_0_1_out_2),
    .C(n4_bit_sync_down_counter_9_0_1_out_3), .D(n4_bit_sync_down_counter_9_0_1_out_4), .c_2(out_7));
  d09 d09_1 (
    .A(n4_bit_sync_down_counter_9_0_1_out_1), .B(n4_bit_sync_down_counter_9_0_1_out_2),
    .C(n4_bit_sync_down_counter_9_0_1_out_3), .D(n4_bit_sync_down_counter_9_0_1_out_4), .d_2(out_6));
  e09 e09_1 (
    .A(n4_bit_sync_down_counter_9_0_1_out_1), .B(n4_bit_sync_down_counter_9_0_1_out_2),
    .C(n4_bit_sync_down_counter_9_0_1_out_3), .D(n4_bit_sync_down_counter_9_0_1_out_4), .e(out_5));
  _7_Segment_Display u_7_segment_display_1 (
    .g(out_1), .f(out_2), .a(out_3), .b(out_4), .e(out_5), .d(out_6), .c(out_7));  // open: dp

  // Notes on the sheet:
  //   2107096
endmodule
