// Logisim project digital clock.circ as structural Verilog
module a09 (
  input  A,
  input  B,
  input  C,
  input  D,
  output a_2
);

  wire not_1_out, xor_1_out;

  not not_1 (not_1_out, xor_1_out);
  xor xor_1 (xor_1_out, B, D);
  or or_1 (a_2, A, C, not_1_out);

  // Notes on the sheet:
  //   a= A + C + BxnorD
endmodule

module b09 (
  input  A,
  input  B,
  input  C,
  input  D,
  output b_2
);

  wire not_1_out, xnor_1_out;

  not not_1 (not_1_out, B);
  xnor xnor_1 (xnor_1_out, C, D);
  or or_1 (b_2, not_1_out, xnor_1_out);

  // Notes on the sheet:
  //   b=B' + CxnorD
endmodule

module c09 (
  input  A,
  input  B,
  input  C,
  input  D,
  output c_2
);

  wire not_1_out;

  not not_1 (not_1_out, C);
  or or_1 (c_2, B, not_1_out, D);

  // Notes on the sheet:
  //   c= B + C' + D
endmodule

module d09 (
  input  A,
  input  B,
  input  C,
  input  D,
  output d_2
);

  wire and_1_out, and_2_out, and_3_out, and_4_out, not_1_out, not_2_out, not_3_out;

  not not_1 (not_1_out, B);
  not not_2 (not_2_out, D);
  not not_3 (not_3_out, C);
  and and_1 (and_1_out, not_2_out, C);
  and and_2 (and_2_out, not_1_out, C);
  and and_3 (and_3_out, not_1_out, not_2_out);
  and and_4 (and_4_out, B, not_3_out, D);
  or or_1 (d_2, A, and_2_out, and_3_out, and_1_out, and_4_out);

  // Notes on the sheet:
  //   2107096
endmodule

module e09 (
  input  A,
  input  B,
  input  C,
  input  D,
  output e
);

  wire and_1_out, and_2_out, not_1_out, not_2_out;

  not not_1 (not_1_out, B);
  not not_2 (not_2_out, D);
  and and_1 (and_1_out, not_1_out, not_2_out);
  and and_2 (and_2_out, C, not_2_out);
  or or_1 (e, and_1_out, and_2_out);
endmodule

// f
module f09 (
  input  A,
  input  B,
  input  C,
  input  D,
  output f
);

  wire and_1_out, and_2_out, and_3_out, not_1_out, not_2_out;

  not not_1 (not_1_out, C);
  not not_2 (not_2_out, D);
  and and_1 (and_1_out, B, not_1_out);
  and and_2 (and_2_out, B, not_2_out);
  and and_3 (and_3_out, not_1_out, not_2_out);
  or or_1 (f, A, and_1_out, and_2_out, and_3_out);
endmodule

module g09 (
  input  A,
  input  B,
  input  C,
  input  D,
  output g
);

  wire and_1_out, not_1_out, xor_1_out;

  not not_1 (not_1_out, D);
  xor xor_1 (xor_1_out, B, C);
  and and_1 (and_1_out, C, not_1_out);
  or or_1 (g, A, xor_1_out, and_1_out);

  // Notes on the sheet:
  //   g=A + CD' + BxorC
endmodule

module _4_bit_sync_up_ctr_0_9_sec (
  input  p_c_input_skip,
  output _3,
  output _2,
  output _1,
  output _0
);

  wire and_1_out, and_2_out, and_3_out, and_4_out, and_5_out, and_6_out, and_7_out, clock_1_out, or_1_out,
       or_2_out, or_3_out, Q0_qn, Q1_qn, Q2_qn, Q3_qn;

  Clock clock_1 (.out(clock_1_out));
  and and_1 (and_1_out, _1, Q0_qn);
  or or_1 (or_1_out, and_1_out, and_2_out);
  and and_2 (and_2_out, Q3_qn, Q1_qn, _0);
  and and_3 (and_3_out, _2, Q1_qn);
  and and_4 (and_4_out, _2, Q0_qn);
  or or_2 (or_2_out, and_3_out, and_4_out, and_5_out);
  and and_5 (and_5_out, Q2_qn, _1, _0);
  and and_6 (and_6_out, _3, Q0_qn);
  or or_3 (or_3_out, and_6_out, and_7_out);
  and and_7 (and_7_out, _2, _1, _0);
  D_Flip_Flop Q0 (.clk(clock_1_out), .D(Q0_qn), .Q(_0), .Qn(Q0_qn), .preset(p_c_input_skip));  // open: en, reset
  D_Flip_Flop Q1 (.clk(clock_1_out), .D(or_1_out), .Q(_1), .Qn(Q1_qn), .preset(p_c_input_skip));  // open: en, reset
  D_Flip_Flop Q2 (.clk(clock_1_out), .D(or_2_out), .Q(_2), .Qn(Q2_qn), .preset(p_c_input_skip));  // open: en, reset
  D_Flip_Flop Q3 (.clk(clock_1_out), .D(or_3_out), .Q(_3), .Qn(Q3_qn), .reset(p_c_input_skip));  // open: preset, en

  // Notes on the sheet:
  //   2107096
endmodule

module _4_bit_async_up_ctr_0_5_min_sec_with_input (
  input  input_0_1,
  output _3,
  output _2,
  output _1,
  output _0
);

  wire _0_qn, _1_qn, _2_qn, and_1_out, and_2_out, and_3_out, and_4_out, not_1_out, or_1_out, or_2_out;

  or or_1 (or_1_out, and_1_out, and_2_out);
  or or_2 (or_2_out, and_3_out, and_4_out);
  and and_1 (and_1_out, _1, _0_qn);
  and and_2 (and_2_out, _2_qn, _1_qn, _0);
  and and_3 (and_3_out, _1, _0);
  and and_4 (and_4_out, _2, _0_qn);
  not not_1 (not_1_out, 1'b1);
  D_Flip_Flop u__0 (.clk(input_0_1), .D(_0_qn), .Q(_0), .Qn(_0_qn));  // open: preset, en, reset
  D_Flip_Flop u__1 (.clk(input_0_1), .D(or_1_out), .Q(_1), .Qn(_1_qn));  // open: preset, en, reset
  D_Flip_Flop u__2 (.clk(input_0_1), .D(or_2_out), .Q(_2), .Qn(_2_qn));  // open: preset, en, reset
  D_Flip_Flop u__3 (.clk(input_0_1), .D(not_1_out), .Q(_3));  // open: Qn, preset, en, reset

  // Notes on the sheet:
  //   2107096
endmodule

module _4_bit_async_up_ctr_0_9_min_with_input (
  input  input_minute,
  input  p_c_input_skip,
  output _3,
  output _2,
  output _1,
  output _0
);

  wire and_1_out, and_2_out, and_3_out, and_4_out, and_5_out, and_6_out, and_7_out, or_1_out, or_2_out,
       or_3_out, Q0_qn, Q1_qn, Q2_qn, Q3_qn;

  and and_1 (and_1_out, _1, Q0_qn);
  or or_1 (or_1_out, and_1_out, and_2_out);
  and and_2 (and_2_out, Q3_qn, Q1_qn, _0);
  and and_3 (and_3_out, _2, Q1_qn);
  or or_2 (or_2_out, and_3_out, and_4_out, and_5_out);
  and and_4 (and_4_out, _2, Q0_qn);
  and and_5 (and_5_out, Q2_qn, _1, _0);
  and and_6 (and_6_out, _3, Q0_qn);
  or or_3 (or_3_out, and_6_out, and_7_out);
  and and_7 (and_7_out, _2, _1, _0);
  D_Flip_Flop Q0 (.clk(input_minute), .D(Q0_qn), .Q(_0), .Qn(Q0_qn), .preset(p_c_input_skip));  // open: en, reset
  D_Flip_Flop Q1 (.clk(input_minute), .D(or_1_out), .Q(_1), .Qn(Q1_qn), .preset(p_c_input_skip));  // open: en, reset
  D_Flip_Flop Q2 (.clk(input_minute), .D(or_2_out), .Q(_2), .Qn(Q2_qn), .preset(p_c_input_skip));  // open: en, reset
  D_Flip_Flop Q3 (.clk(input_minute), .D(or_3_out), .Q(_3), .Qn(Q3_qn), .reset(p_c_input_skip));  // open: preset, en

  // Notes on the sheet:
  //   2107096
endmodule

module _1_bit_async_up_ctr_0_1_hrs_with_input (
  input  \input ,
  input  p_c_input,
  output _0
);

  wire d_ff_1_qn;

  D_Flip_Flop d_ff_1 (.clk(\input ), .D(d_ff_1_qn), .Q(_0), .Qn(d_ff_1_qn), .reset(p_c_input));  // open: preset, en
endmodule

module _4_bit_async_up_ctr_0_9_hrs_with_input (
  input  input_min,
  input  preset_input,
  output out_3,
  output out_4,
  output out_5,
  output out_6
);

  wire and_1_out, and_2_out, and_3_out, and_4_out, and_5_out, and_6_out, and_7_out, or_1_out, or_2_out,
       or_3_out, Q0_qn, Q1_qn, Q2_qn, Q3_qn;

  and and_1 (and_1_out, out_5, Q0_qn);
  or or_1 (or_1_out, and_1_out, and_2_out);
  and and_2 (and_2_out, Q3_qn, Q1_qn, out_6);
  and and_3 (and_3_out, out_4, Q1_qn);
  or or_2 (or_2_out, and_3_out, and_4_out, and_5_out);
  and and_4 (and_4_out, out_4, Q0_qn);
  and and_5 (and_5_out, Q2_qn, out_5, out_6);
  and and_6 (and_6_out, out_3, Q0_qn);
  or or_3 (or_3_out, and_6_out, and_7_out);
  and and_7 (and_7_out, out_4, out_5, out_6);
  D_Flip_Flop Q0 (.clk(input_min), .D(Q0_qn), .Q(out_6), .Qn(Q0_qn), .preset(preset_input));  // open: en, reset
  D_Flip_Flop Q1 (.clk(input_min), .D(or_1_out), .Q(out_5), .Qn(Q1_qn), .reset(preset_input));  // open: preset, en
  D_Flip_Flop Q2 (.clk(input_min), .D(or_2_out), .Q(out_4), .Qn(Q2_qn), .reset(preset_input));  // open: preset, en
  D_Flip_Flop Q3 (.clk(input_min), .D(or_3_out), .Q(out_3), .Qn(Q3_qn), .reset(preset_input));  // open: preset, en

  // Notes on the sheet:
  //   2107096
endmodule

module am_pm_async_ctr (
  input  in_1,
  output out_2
);

  wire d_ff_1_qn;

  D_Flip_Flop d_ff_1 (.clk(in_1), .D(d_ff_1_qn), .Q(out_2), .Qn(d_ff_1_qn));  // open: preset, en, reset
endmodule

module _7_segment_input_circuit (
  input  in_1,
  input  in_2,
  input  in_3,
  input  in_4,
  output out_5,
  output out_6,
  output out_7,
  output out_8,
  output out_9,
  output out_10,
  output out_11
);

  a09 a09_1 (.A(in_1), .B(in_2), .C(in_3), .D(in_4), .a_2(out_7));
  b09 b09_1 (.A(in_1), .B(in_2), .C(in_3), .D(in_4), .b_2(out_8));
  f09 f09_1 (.A(in_1), .B(in_2), .C(in_3), .D(in_4), .f(out_6));
  g09 g09_1 (.A(in_1), .B(in_2), .C(in_3), .D(in_4), .g(out_5));
  c09 c09_1 (.A(in_1), .B(in_2), .C(in_3), .D(in_4), .c_2(out_11));
  d09 d09_1 (.A(in_1), .B(in_2), .C(in_3), .D(in_4), .d_2(out_10));
  e09 e09_1 (.A(in_1), .B(in_2), .C(in_3), .D(in_4), .e(out_9));
  _7_Segment_Display u_7_segment_display_1 (
    .g(out_5), .f(out_6), .a(out_7), .b(out_8), .e(out_9), .d(out_10), .c(out_11));  // open: dp

  // Notes on the sheet:
  //   2107096
endmodule

module digital_clock (
);

  wire am_pm_async_ctr_1_out_2, and_1_out, and_2_out, and_3_out, and_4_out,
       n1_bit_async_up_ctr_0_1_hrs_with_input_1__0, n4_bit_async_up_ctr_0_5_min_sec_with_input_1__0,
       n4_bit_async_up_ctr_0_5_min_sec_with_input_1__1, n4_bit_async_up_ctr_0_5_min_sec_with_input_1__2,
       n4_bit_async_up_ctr_0_5_min_sec_with_input_1__3, n4_bit_async_up_ctr_0_5_min_sec_with_input_2__0,
       n4_bit_async_up_ctr_0_5_min_sec_with_input_2__1, n4_bit_async_up_ctr_0_5_min_sec_with_input_2__2,
       n4_bit_async_up_ctr_0_5_min_sec_with_input_2__3, n4_bit_async_up_ctr_0_9_hrs_with_input_1_out_3,
       n4_bit_async_up_ctr_0_9_hrs_with_input_1_out_4, n4_bit_async_up_ctr_0_9_hrs_with_input_1_out_5,
       n4_bit_async_up_ctr_0_9_hrs_with_input_1_out_6, n4_bit_async_up_ctr_0_9_min_with_input_1__0,
       n4_bit_async_up_ctr_0_9_min_with_input_1__1, n4_bit_async_up_ctr_0_9_min_with_input_1__2,
       n4_bit_async_up_ctr_0_9_min_with_input_1__3, n4_bit_sync_up_ctr_0_9_sec_1__0,
       n4_bit_sync_up_ctr_0_9_sec_1__1, n4_bit_sync_up_ctr_0_9_sec_1__2, n4_bit_sync_up_ctr_0_9_sec_1__3,
       n7_segment_input_circuit_1_out_5, n7_segment_input_circuit_1_out_6, n7_segment_input_circuit_1_out_7,
       n7_segment_input_circuit_1_out_8, n7_segment_input_circuit_2_out_9, n7_segment_input_circuit_2_out_10,
       n7_segment_input_circuit_2_out_11, n7_segment_input_circuit_3_out_5, n7_segment_input_circuit_3_out_6,
       n7_segment_input_circuit_3_out_7, n7_segment_input_circuit_3_out_8, n7_segment_input_circuit_4_out_9,
       n7_segment_input_circuit_4_out_10, n7_segment_input_circuit_4_out_11,
       n7_segment_input_circuit_5_out_5, n7_segment_input_circuit_5_out_6, n7_segment_input_circuit_5_out_7,
       n7_segment_input_circuit_5_out_8, n7_segment_input_circuit_6_out_9, n7_segment_input_circuit_6_out_10,
       n7_segment_input_circuit_6_out_11, n7_segment_input_circuit_7_out_5, n7_segment_input_circuit_7_out_6,
       n7_segment_input_circuit_7_out_7, n7_segment_input_circuit_7_out_8, n7_segment_input_circuit_8_out_9,
       n7_segment_input_circuit_8_out_10, n7_segment_input_circuit_8_out_11,
       n7_segment_input_circuit_9_out_5, n7_segment_input_circuit_9_out_6, n7_segment_input_circuit_9_out_7,
       n7_segment_input_circuit_9_out_8, n7_segment_input_circuit_10_out_9,
       n7_segment_input_circuit_10_out_10, n7_segment_input_circuit_10_out_11,
       n7_segment_input_circuit_11_out_5, n7_segment_input_circuit_11_out_6,
       n7_segment_input_circuit_11_out_7, n7_segment_input_circuit_11_out_8,
       n7_segment_input_circuit_12_out_9, n7_segment_input_circuit_12_out_10,
       n7_segment_input_circuit_12_out_11, nor_1_out, nor_2_out, nor_3_out, nor_4_out, nor_5_out, not_1_out,
       not_2_out, not_3_out, not_4_out, not_5_out, not_6_out, not_7_out, not_8_out, not_9_out, not_10_out,
       not_11_out, not_12_out, not_13_out, not_14_out;

  not not_1 (not_1_out, 1'b1);
  not not_2 (not_2_out, n4_bit_async_up_ctr_0_9_hrs_with_input_1_out_3);
  not not_3 (not_3_out, n4_bit_async_up_ctr_0_9_hrs_with_input_1_out_4);
  and and_1 (and_1_out, n1_bit_async_up_ctr_0_1_hrs_with_input_1__0, not_2_out, not_3_out, n4_bit_async_up_ctr_0_9_hrs_with_input_1_out_5, n4_bit_async_up_ctr_0_9_hrs_with_input_1_out_6);
  _1_bit_async_up_ctr_0_1_hrs_with_input u_1_bit_async_up_ctr_0_1_hrs_with_input_1 (
    .\input (nor_1_out), .p_c_input(and_1_out), ._0(n1_bit_async_up_ctr_0_1_hrs_with_input_1__0));
  nor nor_1 (nor_1_out, n4_bit_async_up_ctr_0_9_hrs_with_input_1_out_6, n4_bit_async_up_ctr_0_9_hrs_with_input_1_out_5, n4_bit_async_up_ctr_0_9_hrs_with_input_1_out_4, n4_bit_async_up_ctr_0_9_hrs_with_input_1_out_3);
  not not_4 (not_4_out, n4_bit_async_up_ctr_0_9_hrs_with_input_1_out_3);
  and and_2 (and_2_out, n1_bit_async_up_ctr_0_1_hrs_with_input_1__0, not_4_out, not_5_out, n4_bit_async_up_ctr_0_9_hrs_with_input_1_out_5, not_6_out);
  not not_5 (not_5_out, n4_bit_async_up_ctr_0_9_hrs_with_input_1_out_4);
  not not_6 (not_6_out, n4_bit_async_up_ctr_0_9_hrs_with_input_1_out_6);
  _7_segment_input_circuit u_7_segment_input_circuit_1 (
    .in_1(not_1_out), .in_2(not_1_out), .in_3(not_1_out), .in_4(n1_bit_async_up_ctr_0_1_hrs_with_input_1__0),
    .out_5(n7_segment_input_circuit_1_out_5), .out_6(n7_segment_input_circuit_1_out_6),
    .out_7(n7_segment_input_circuit_1_out_7), .out_8(n7_segment_input_circuit_1_out_8));  // open: out_9, out_10, out_11
  _7_Segment_Display u_7_segment_display_1 (
    .g(n7_segment_input_circuit_1_out_5), .f(n7_segment_input_circuit_1_out_6),
    .a(n7_segment_input_circuit_1_out_7), .b(n7_segment_input_circuit_1_out_8),
    .e(n7_segment_input_circuit_2_out_9), .d(n7_segment_input_circuit_2_out_10),
    .c(n7_segment_input_circuit_2_out_11));  // open: dp
  _7_segment_input_circuit u_7_segment_input_circuit_2 (
    .in_1(not_1_out), .in_2(not_1_out), .in_3(not_1_out), .in_4(n1_bit_async_up_ctr_0_1_hrs_with_input_1__0),
    .out_9(n7_segment_input_circuit_2_out_9), .out_10(n7_segment_input_circuit_2_out_10),
    .out_11(n7_segment_input_circuit_2_out_11));  // open: out_5, out_6, out_7, out_8
  _4_bit_async_up_ctr_0_9_hrs_with_input u_4_bit_async_up_ctr_0_9_hrs_with_input_1 (
    .input_min(nor_2_out), .preset_input(and_1_out), .out_3(n4_bit_async_up_ctr_0_9_hrs_with_input_1_out_3),
    .out_4(n4_bit_async_up_ctr_0_9_hrs_with_input_1_out_4),
    .out_5(n4_bit_async_up_ctr_0_9_hrs_with_input_1_out_5),
    .out_6(n4_bit_async_up_ctr_0_9_hrs_with_input_1_out_6));
  nor nor_2 (nor_2_out, n4_bit_async_up_ctr_0_5_min_sec_with_input_1__3, n4_bit_async_up_ctr_0_5_min_sec_with_input_1__2, n4_bit_async_up_ctr_0_5_min_sec_with_input_1__1, n4_bit_async_up_ctr_0_5_min_sec_with_input_1__0);
  _7_segment_input_circuit u_7_segment_input_circuit_3 (
    .in_1(n4_bit_async_up_ctr_0_9_hrs_with_input_1_out_3),
    .in_2(n4_bit_async_up_ctr_0_9_hrs_with_input_1_out_4),
    .in_3(n4_bit_async_up_ctr_0_9_hrs_with_input_1_out_5),
    .in_4(n4_bit_async_up_ctr_0_9_hrs_with_input_1_out_6), .out_5(n7_segment_input_circuit_3_out_5),
    .out_6(n7_segment_input_circuit_3_out_6), .out_7(n7_segment_input_circuit_3_out_7),
    .out_8(n7_segment_input_circuit_3_out_8));  // open: out_9, out_10, out_11
  _7_Segment_Display u_7_segment_display_2 (
    .g(n7_segment_input_circuit_3_out_5), .f(n7_segment_input_circuit_3_out_6),
    .a(n7_segment_input_circuit_3_out_7), .b(n7_segment_input_circuit_3_out_8),
    .e(n7_segment_input_circuit_4_out_9), .d(n7_segment_input_circuit_4_out_10),
    .c(n7_segment_input_circuit_4_out_11), .dp(am_pm_async_ctr_1_out_2));
  _7_segment_input_circuit u_7_segment_input_circuit_4 (
    .in_1(n4_bit_async_up_ctr_0_9_hrs_with_input_1_out_3),
    .in_2(n4_bit_async_up_ctr_0_9_hrs_with_input_1_out_4),
    .in_3(n4_bit_async_up_ctr_0_9_hrs_with_input_1_out_5),
    .in_4(n4_bit_async_up_ctr_0_9_hrs_with_input_1_out_6), .out_9(n7_segment_input_circuit_4_out_9),
    .out_10(n7_segment_input_circuit_4_out_10), .out_11(n7_segment_input_circuit_4_out_11));  // open: out_5, out_6, out_7, out_8
  am_pm_async_ctr am_pm_async_ctr_1 (.in_1(and_2_out), .out_2(am_pm_async_ctr_1_out_2));
  not not_7 (not_7_out, n4_bit_async_up_ctr_0_5_min_sec_with_input_1__3);
  and and_3 (and_3_out, not_7_out, not_8_out, n4_bit_async_up_ctr_0_5_min_sec_with_input_1__1, n4_bit_async_up_ctr_0_5_min_sec_with_input_1__0, not_9_out, n4_bit_async_up_ctr_0_9_min_with_input_1__2, n4_bit_async_up_ctr_0_9_min_with_input_1__1, not_10_out);
  not not_8 (not_8_out, n4_bit_async_up_ctr_0_5_min_sec_with_input_1__2);
  not not_9 (not_9_out, n4_bit_async_up_ctr_0_9_min_with_input_1__3);
  not not_10 (not_10_out, n4_bit_async_up_ctr_0_9_min_with_input_1__0);
  nor nor_3 (nor_3_out, n4_bit_async_up_ctr_0_9_min_with_input_1__3, n4_bit_async_up_ctr_0_9_min_with_input_1__2, n4_bit_async_up_ctr_0_9_min_with_input_1__1, n4_bit_async_up_ctr_0_9_min_with_input_1__0);
  _4_bit_async_up_ctr_0_5_min_sec_with_input u_4_bit_async_up_ctr_0_5_min_sec_with_input_1 (
    .input_0_1(nor_3_out), ._3(n4_bit_async_up_ctr_0_5_min_sec_with_input_1__3),
    ._2(n4_bit_async_up_ctr_0_5_min_sec_with_input_1__2),
    ._1(n4_bit_async_up_ctr_0_5_min_sec_with_input_1__1), ._0(n4_bit_async_up_ctr_0_5_min_sec_with_input_1__0));
  _7_segment_input_circuit u_7_segment_input_circuit_5 (
    .in_1(n4_bit_async_up_ctr_0_5_min_sec_with_input_1__3),
    .in_2(n4_bit_async_up_ctr_0_5_min_sec_with_input_1__2),
    .in_3(n4_bit_async_up_ctr_0_5_min_sec_with_input_1__1),
    .in_4(n4_bit_async_up_ctr_0_5_min_sec_with_input_1__0), .out_5(n7_segment_input_circuit_5_out_5),
    .out_6(n7_segment_input_circuit_5_out_6), .out_7(n7_segment_input_circuit_5_out_7),
    .out_8(n7_segment_input_circuit_5_out_8));  // open: out_9, out_10, out_11
  _7_Segment_Display u_7_segment_display_3 (
    .g(n7_segment_input_circuit_5_out_5), .f(n7_segment_input_circuit_5_out_6),
    .a(n7_segment_input_circuit_5_out_7), .b(n7_segment_input_circuit_5_out_8),
    .e(n7_segment_input_circuit_6_out_9), .d(n7_segment_input_circuit_6_out_10),
    .c(n7_segment_input_circuit_6_out_11));  // open: dp
  _7_segment_input_circuit u_7_segment_input_circuit_6 (
    .in_1(n4_bit_async_up_ctr_0_5_min_sec_with_input_1__3),
    .in_2(n4_bit_async_up_ctr_0_5_min_sec_with_input_1__2),
    .in_3(n4_bit_async_up_ctr_0_5_min_sec_with_input_1__1),
    .in_4(n4_bit_async_up_ctr_0_5_min_sec_with_input_1__0), .out_9(n7_segment_input_circuit_6_out_9),
    .out_10(n7_segment_input_circuit_6_out_10), .out_11(n7_segment_input_circuit_6_out_11));  // open: out_5, out_6, out_7, out_8
  _7_segment_input_circuit u_7_segment_input_circuit_7 (
    .in_1(n4_bit_async_up_ctr_0_9_min_with_input_1__3), .in_2(n4_bit_async_up_ctr_0_9_min_with_input_1__2),
    .in_3(n4_bit_async_up_ctr_0_9_min_with_input_1__1), .in_4(n4_bit_async_up_ctr_0_9_min_with_input_1__0),
    .out_5(n7_segment_input_circuit_7_out_5), .out_6(n7_segment_input_circuit_7_out_6),
    .out_7(n7_segment_input_circuit_7_out_7), .out_8(n7_segment_input_circuit_7_out_8));  // open: out_9, out_10, out_11
  _7_Segment_Display u_7_segment_display_4 (
    .g(n7_segment_input_circuit_7_out_5), .f(n7_segment_input_circuit_7_out_6),
    .a(n7_segment_input_circuit_7_out_7), .b(n7_segment_input_circuit_7_out_8),
    .e(n7_segment_input_circuit_8_out_9), .d(n7_segment_input_circuit_8_out_10),
    .c(n7_segment_input_circuit_8_out_11));  // open: dp
  _7_segment_input_circuit u_7_segment_input_circuit_8 (
    .in_1(n4_bit_async_up_ctr_0_9_min_with_input_1__3), .in_2(n4_bit_async_up_ctr_0_9_min_with_input_1__2),
    .in_3(n4_bit_async_up_ctr_0_9_min_with_input_1__1), .in_4(n4_bit_async_up_ctr_0_9_min_with_input_1__0),
    .out_9(n7_segment_input_circuit_8_out_9), .out_10(n7_segment_input_circuit_8_out_10),
    .out_11(n7_segment_input_circuit_8_out_11));  // open: out_5, out_6, out_7, out_8
  _4_bit_async_up_ctr_0_9_min_with_input u_4_bit_async_up_ctr_0_9_min_with_input_1 (
    .input_minute(nor_4_out), .p_c_input_skip(and_3_out), ._3(n4_bit_async_up_ctr_0_9_min_with_input_1__3),
    ._2(n4_bit_async_up_ctr_0_9_min_with_input_1__2), ._1(n4_bit_async_up_ctr_0_9_min_with_input_1__1),
    ._0(n4_bit_async_up_ctr_0_9_min_with_input_1__0));
  and and_4 (and_4_out, not_11_out, not_12_out, n4_bit_async_up_ctr_0_5_min_sec_with_input_2__1, n4_bit_async_up_ctr_0_5_min_sec_with_input_2__0, not_13_out, n4_bit_sync_up_ctr_0_9_sec_1__2, n4_bit_sync_up_ctr_0_9_sec_1__1, not_14_out);
  nor nor_4 (nor_4_out, n4_bit_async_up_ctr_0_5_min_sec_with_input_2__3, n4_bit_async_up_ctr_0_5_min_sec_with_input_2__2, n4_bit_async_up_ctr_0_5_min_sec_with_input_2__1, n4_bit_async_up_ctr_0_5_min_sec_with_input_2__0);
  not not_11 (not_11_out, n4_bit_async_up_ctr_0_5_min_sec_with_input_2__3);
  not not_12 (not_12_out, n4_bit_async_up_ctr_0_5_min_sec_with_input_2__2);
  not not_13 (not_13_out, n4_bit_sync_up_ctr_0_9_sec_1__3);
  not not_14 (not_14_out, n4_bit_sync_up_ctr_0_9_sec_1__0);
  _4_bit_async_up_ctr_0_5_min_sec_with_input u_4_bit_async_up_ctr_0_5_min_sec_with_input_2 (
    .input_0_1(nor_5_out), ._3(n4_bit_async_up_ctr_0_5_min_sec_with_input_2__3),
    ._2(n4_bit_async_up_ctr_0_5_min_sec_with_input_2__2),
    ._1(n4_bit_async_up_ctr_0_5_min_sec_with_input_2__1), ._0(n4_bit_async_up_ctr_0_5_min_sec_with_input_2__0));
  nor nor_5 (nor_5_out, n4_bit_sync_up_ctr_0_9_sec_1__3, n4_bit_sync_up_ctr_0_9_sec_1__2, n4_bit_sync_up_ctr_0_9_sec_1__1, n4_bit_sync_up_ctr_0_9_sec_1__0);
  _7_segment_input_circuit u_7_segment_input_circuit_9 (
    .in_1(n4_bit_async_up_ctr_0_5_min_sec_with_input_2__3),
    .in_2(n4_bit_async_up_ctr_0_5_min_sec_with_input_2__2),
    .in_3(n4_bit_async_up_ctr_0_5_min_sec_with_input_2__1),
    .in_4(n4_bit_async_up_ctr_0_5_min_sec_with_input_2__0), .out_5(n7_segment_input_circuit_9_out_5),
    .out_6(n7_segment_input_circuit_9_out_6), .out_7(n7_segment_input_circuit_9_out_7),
    .out_8(n7_segment_input_circuit_9_out_8));  // open: out_9, out_10, out_11
  _7_Segment_Display u_7_segment_display_5 (
    .g(n7_segment_input_circuit_9_out_5), .f(n7_segment_input_circuit_9_out_6),
    .a(n7_segment_input_circuit_9_out_7), .b(n7_segment_input_circuit_9_out_8),
    .e(n7_segment_input_circuit_10_out_9), .d(n7_segment_input_circuit_10_out_10),
    .c(n7_segment_input_circuit_10_out_11));  // open: dp
  _7_segment_input_circuit u_7_segment_input_circuit_10 (
    .in_1(n4_bit_async_up_ctr_0_5_min_sec_with_input_2__3),
    .in_2(n4_bit_async_up_ctr_0_5_min_sec_with_input_2__2),
    .in_3(n4_bit_async_up_ctr_0_5_min_sec_with_input_2__1),
    .in_4(n4_bit_async_up_ctr_0_5_min_sec_with_input_2__0), .out_9(n7_segment_input_circuit_10_out_9),
    .out_10(n7_segment_input_circuit_10_out_10), .out_11(n7_segment_input_circuit_10_out_11));  // open: out_5, out_6, out_7, out_8
  _4_bit_sync_up_ctr_0_9_sec u_4_bit_sync_up_ctr_0_9_sec_1 (
    .p_c_input_skip(and_4_out), ._3(n4_bit_sync_up_ctr_0_9_sec_1__3), ._2(n4_bit_sync_up_ctr_0_9_sec_1__2),
    ._1(n4_bit_sync_up_ctr_0_9_sec_1__1), ._0(n4_bit_sync_up_ctr_0_9_sec_1__0));
  _7_segment_input_circuit u_7_segment_input_circuit_11 (
    .in_1(n4_bit_sync_up_ctr_0_9_sec_1__3), .in_2(n4_bit_sync_up_ctr_0_9_sec_1__2),
    .in_3(n4_bit_sync_up_ctr_0_9_sec_1__1), .in_4(n4_bit_sync_up_ctr_0_9_sec_1__0),
    .out_5(n7_segment_input_circuit_11_out_5), .out_6(n7_segment_input_circuit_11_out_6),
    .out_7(n7_segment_input_circuit_11_out_7), .out_8(n7_segment_input_circuit_11_out_8));  // open: out_9, out_10, out_11
  _7_Segment_Display u_7_segment_display_6 (
    .g(n7_segment_input_circuit_11_out_5), .f(n7_segment_input_circuit_11_out_6),
    .a(n7_segment_input_circuit_11_out_7), .b(n7_segment_input_circuit_11_out_8),
    .e(n7_segment_input_circuit_12_out_9), .d(n7_segment_input_circuit_12_out_10),
    .c(n7_segment_input_circuit_12_out_11));  // open: dp
  _7_segment_input_circuit u_7_segment_input_circuit_12 (
    .in_1(n4_bit_sync_up_ctr_0_9_sec_1__3), .in_2(n4_bit_sync_up_ctr_0_9_sec_1__2),
    .in_3(n4_bit_sync_up_ctr_0_9_sec_1__1), .in_4(n4_bit_sync_up_ctr_0_9_sec_1__0),
    .out_9(n7_segment_input_circuit_12_out_9), .out_10(n7_segment_input_circuit_12_out_10),
    .out_11(n7_segment_input_circuit_12_out_11));  // open: out_5, out_6, out_7, out_8

  // Notes on the sheet:
  //   2107096
  //   HOURS
  //   MINUTES
  //   SECONDS
endmodule
