// Logisim project hexato7.circ as structural Verilog: 12 circuits, main circuit main
module main (
);

  wire hexa_to_7seg_reverse_1_out_4, hexa_to_7seg_reverse_1_out_5, hexa_to_7seg_reverse_1_out_6,
       hexa_to_7seg_reverse_1_out_7, hexa_to_7seg_reverse_2_out_1, hexa_to_7seg_reverse_2_out_2,
       hexa_to_7seg_reverse_2_out_3;

  hexa_to_7seg_reverse hexa_to_7seg_reverse_1 (
    .out_4(hexa_to_7seg_reverse_1_out_4), .out_5(hexa_to_7seg_reverse_1_out_5),
    .out_6(hexa_to_7seg_reverse_1_out_6), .out_7(hexa_to_7seg_reverse_1_out_7));  // open: out_1, out_2, out_3
  _7_Segment_Display u_7_segment_display_1 (
    .g(hexa_to_7seg_reverse_1_out_4), .f(hexa_to_7seg_reverse_1_out_5), .a(hexa_to_7seg_reverse_1_out_6),
    .b(hexa_to_7seg_reverse_1_out_7), .e(hexa_to_7seg_reverse_2_out_1), .d(hexa_to_7seg_reverse_2_out_2),
    .c(hexa_to_7seg_reverse_2_out_3));  // open: dp
  hexa_to_7seg_reverse hexa_to_7seg_reverse_2 (
    .out_1(hexa_to_7seg_reverse_2_out_1), .out_2(hexa_to_7seg_reverse_2_out_2),
    .out_3(hexa_to_7seg_reverse_2_out_3));  // open: out_4, out_5, out_6, out_7

  // Notes on the sheet:
  //   2107096
endmodule

module a (
  input  A,
  input  B,
  input  C,
  input  D,
  output a_2
);

  wire and_1_out, and_2_out, and_3_out, and_4_out, and_5_out, and_6_out, not_1_out, not_2_out, not_3_out,
       not_4_out;

  not not_1 (not_1_out, B);
  not not_2 (not_2_out, D);
  not not_3 (not_3_out, A);
  not not_4 (not_4_out, C);
  and and_1 (and_1_out, not_1_out, not_2_out);
  and and_2 (and_2_out, A, not_2_out);
  and and_3 (and_3_out, not_3_out, C);
  and and_4 (and_4_out, A, B, C);
  and and_5 (and_5_out, A, not_1_out, not_4_out);
  and and_6 (and_6_out, not_3_out, B, D);
  or or_1 (a_2, and_1_out, and_2_out, and_3_out, and_4_out, and_5_out, and_6_out);
endmodule

module b (
  input  A,
  input  B,
  input  C,
  input  D,
  output b_2
);

  wire and_1_out, and_2_out, and_3_out, and_4_out, and_5_out, and_6_out, not_1_out, not_2_out, not_3_out,
       not_4_out;

  not not_1 (not_1_out, A);
  not not_2 (not_2_out, B);
  not not_3 (not_3_out, C);
  not not_4 (not_4_out, D);
  and and_1 (and_1_out, not_1_out, not_2_out);
  and and_2 (and_2_out, not_2_out, not_3_out);
  and and_3 (and_3_out, not_1_out, not_3_out, not_4_out);
  and and_4 (and_4_out, not_1_out, C, D);
  and and_5 (and_5_out, A, not_3_out, D);
  and and_6 (and_6_out, not_2_out, not_4_out);
  or or_1 (b_2, and_1_out, and_2_out, and_3_out, and_4_out, and_5_out, and_6_out);
endmodule

module c (
  input  A,
  input  B,
  input  C,
  input  D,
  output c_2
);

  wire and_1_out, and_2_out, and_3_out, and_4_out, and_5_out, not_1_out, not_2_out, not_3_out;

  not not_1 (not_1_out, A);
  not not_2 (not_2_out, B);
  not not_3 (not_3_out, C);
  and and_1 (and_1_out, not_2_out, not_3_out);
  and and_2 (and_2_out, not_3_out, D);
  and and_3 (and_3_out, not_1_out, B);
  and and_4 (and_4_out, A, not_2_out);
  and and_5 (and_5_out, not_1_out, D);
  or or_1 (c_2, and_3_out, and_1_out, and_5_out, and_4_out, and_2_out);
endmodule

module d (
  input  A,
  input  B,
  input  C,
  input  D,
  output d_2
);

  wire and_1_out, and_2_out, and_3_out, and_4_out, and_5_out, not_1_out, not_2_out, not_3_out, not_4_out;

  not not_1 (not_1_out, C);
  not not_2 (not_2_out, A);
  not not_3 (not_3_out, B);
  not not_4 (not_4_out, D);
  and and_1 (and_1_out, not_3_out, C, D);
  and and_2 (and_2_out, B, D, not_1_out);
  and and_3 (and_3_out, A, not_1_out);
  and and_4 (and_4_out, B, C, not_4_out);
  and and_5 (and_5_out, not_2_out, not_3_out, not_4_out);
  or or_1 (d_2, and_5_out, and_1_out, and_2_out, and_3_out, and_4_out);
endmodule

module e (
  input  A,
  input  B,
  input  C,
  input  D,
  output e
);

  wire and_1_out, and_2_out, and_3_out, and_4_out, not_1_out, not_2_out;

  not not_1 (not_1_out, B);
  not not_2 (not_2_out, D);
  and and_1 (and_1_out, A, B);
  and and_2 (and_2_out, not_1_out, not_2_out);
  and and_3 (and_3_out, C, not_2_out);
  and and_4 (and_4_out, A, C);
  or or_1 (e, and_2_out, and_1_out, and_3_out, and_4_out);
endmodule

module f (
  input  A,
  input  B,
  input  C,
  input  D,
  output f
);

  wire and_1_out, and_2_out, and_3_out, and_4_out, and_5_out, not_1_out, not_2_out, not_3_out, not_4_out;

  not not_1 (not_1_out, B);
  and and_1 (and_1_out, A, not_1_out);
  and and_2 (and_2_out, A, C);
  not not_2 (not_2_out, C);
  and and_3 (and_3_out, not_2_out, not_3_out);
  not not_3 (not_3_out, D);
  not not_4 (not_4_out, A);
  and and_4 (and_4_out, not_4_out, B, not_2_out);
  and and_5 (and_5_out, B, C, not_3_out);
  or or_1 (f, and_5_out, and_4_out, and_2_out, and_1_out, and_3_out);
endmodule

module g (
  input  A,
  input  B,
  input  C,
  input  D,
  output g
);

  wire and_1_out, and_2_out, and_3_out, and_4_out, and_5_out, and_6_out, not_1_out, not_2_out, not_3_out,
       not_4_out;

  not not_1 (not_1_out, B);
  not not_2 (not_2_out, A);
  not not_3 (not_3_out, C);
  not not_4 (not_4_out, D);
  and and_1 (and_1_out, A, C);
  and and_2 (and_2_out, A, not_1_out);
  and and_3 (and_3_out, not_1_out, C);
  and and_4 (and_4_out, A, D);
  and and_5 (and_5_out, not_2_out, not_3_out, B);
  and and_6 (and_6_out, C, not_4_out);
  or or_1 (g, and_1_out, and_2_out, and_3_out, and_4_out, and_5_out, and_6_out);
endmodule

module _4_bit_up_sync_counter (
  output out_1,
  output out_2,
  output out_3,
  output out_4
);

  wire and_1_out, and_2_out, and_3_out, and_4_out, and_5_out, and_6_out, and_7_out, clock_1_out, d_ff_1_qn,
       d_ff_2_qn, d_ff_3_qn, d_ff_4_qn, or_1_out, or_2_out, xor_1_out;

  Clock clock_1 (.out(clock_1_out));
  xor xor_1 (xor_1_out, out_1, out_2);
  or or_1 (or_1_out, and_1_out, and_2_out, and_3_out);
  or or_2 (or_2_out, and_4_out, and_5_out, and_6_out, and_7_out);
  and and_1 (and_1_out, out_3, d_ff_2_qn);
  and and_2 (and_2_out, out_3, d_ff_1_qn);
  and and_3 (and_3_out, out_1, out_2, d_ff_3_qn);
  and and_4 (and_4_out, out_4, d_ff_3_qn);
  and and_5 (and_5_out, out_4, d_ff_2_qn);
  and and_6 (and_6_out, out_4, d_ff_1_qn);
  and and_7 (and_7_out, d_ff_4_qn, out_3, out_2, out_1);
  D_Flip_Flop d_ff_1 (.clk(clock_1_out), .D(d_ff_1_qn), .Q(out_1), .Qn(d_ff_1_qn));  // open: preset, en, reset
  D_Flip_Flop d_ff_2 (.clk(clock_1_out), .D(xor_1_out), .Q(out_2), .Qn(d_ff_2_qn));  // open: preset, en, reset
  D_Flip_Flop d_ff_3 (.clk(clock_1_out), .D(or_1_out), .Q(out_3), .Qn(d_ff_3_qn));  // open: preset, en, reset
  D_Flip_Flop d_ff_4 (.clk(clock_1_out), .D(or_2_out), .Q(out_4), .Qn(d_ff_4_qn));  // open: preset, en, reset
endmodule

module _4_bit_down_sync_counter (
  output out_1,
  output out_2,
  output out_3,
  output out_4
);

  wire _0_qn, _1_qn, _2_qn, _3_qn, and_1_out, and_2_out, and_3_out, and_4_out, and_5_out, and_6_out,
       and_7_out, and_8_out, and_9_out, clock_1_out, or_1_out, or_2_out, or_3_out;

  or or_1 (or_1_out, and_1_out, and_2_out);
  or or_2 (or_2_out, and_3_out, and_4_out, and_5_out);
  or or_3 (or_3_out, and_6_out, and_7_out, and_8_out, and_9_out);
  and and_1 (and_1_out, _0_qn, _1_qn);
  and and_2 (and_2_out, out_4, out_3);
  and and_3 (and_3_out, _0_qn, _1_qn, _2_qn);
  and and_4 (and_4_out, out_4, out_2);
  and and_5 (and_5_out, out_3, out_2);
  and and_6 (and_6_out, out_1, out_2);
  and and_7 (and_7_out, out_1, out_3);
  and and_8 (and_8_out, out_1, out_4);
  and and_9 (and_9_out, _3_qn, _2_qn, _1_qn, _0_qn);
  Clock clock_1 (.out(clock_1_out));
  D_Flip_Flop _0 (.clk(clock_1_out), .D(_0_qn), .Q(out_4), .Qn(_0_qn));  // open: preset, en, reset
  D_Flip_Flop _1 (.clk(clock_1_out), .D(or_1_out), .Q(out_3), .Qn(_1_qn));  // open: preset, en, reset
  D_Flip_Flop _2 (.clk(clock_1_out), .D(or_2_out), .Q(out_2), .Qn(_2_qn));  // open: preset, en, reset
  D_Flip_Flop _3 (.clk(clock_1_out), .D(or_3_out), .Q(out_1), .Qn(_3_qn));  // open: preset, en, reset

  // Notes on the sheet:
  //   2107096
  //   D3 = Q3Q2 + Q3Q1 + Q3Q0 + Q3'Q2'Q1'Q0'
  //   D0 = Q0'
  //   D1 = Q1Q0 + Q1'Q0'
  //   D2 = Q2Q1 + Q2Q0 + Q2'Q1'Q0'
endmodule

module hexa_to_7seg (
  output out_1,
  output out_2,
  output out_3,
  output out_4,
  output out_5,
  output out_6,
  output out_7
);

  wire n4_bit_up_sync_counter_1_out_1, n4_bit_up_sync_counter_1_out_2, n4_bit_up_sync_counter_1_out_3,
       n4_bit_up_sync_counter_1_out_4;

  _4_bit_up_sync_counter u_4_bit_up_sync_counter_1 (
    .out_1(n4_bit_up_sync_counter_1_out_1), .out_2(n4_bit_up_sync_counter_1_out_2),
    .out_3(n4_bit_up_sync_counter_1_out_3), .out_4(n4_bit_up_sync_counter_1_out_4));
  b b_1 (
    .A(n4_bit_up_sync_counter_1_out_4), .B(n4_bit_up_sync_counter_1_out_3),
    .C(n4_bit_up_sync_counter_1_out_2), .D(n4_bit_up_sync_counter_1_out_1), .b_2(out_7));
  a a_1 (
    .A(n4_bit_up_sync_counter_1_out_4), .B(n4_bit_up_sync_counter_1_out_3),
    .C(n4_bit_up_sync_counter_1_out_2), .D(n4_bit_up_sync_counter_1_out_1), .a_2(out_6));
  f f_1 (
    .A(n4_bit_up_sync_counter_1_out_4), .B(n4_bit_up_sync_counter_1_out_3),
    .C(n4_bit_up_sync_counter_1_out_2), .D(n4_bit_up_sync_counter_1_out_1), .f(out_5));
  g g_1 (
    .A(n4_bit_up_sync_counter_1_out_4), .B(n4_bit_up_sync_counter_1_out_3),
    .C(n4_bit_up_sync_counter_1_out_2), .D(n4_bit_up_sync_counter_1_out_1), .g(out_4));
  e e_1 (
    .A(n4_bit_up_sync_counter_1_out_4), .B(n4_bit_up_sync_counter_1_out_3),
    .C(n4_bit_up_sync_counter_1_out_2), .D(n4_bit_up_sync_counter_1_out_1), .e(out_1));
  d d_1 (
    .A(n4_bit_up_sync_counter_1_out_4), .B(n4_bit_up_sync_counter_1_out_3),
    .C(n4_bit_up_sync_counter_1_out_2), .D(n4_bit_up_sync_counter_1_out_1), .d_2(out_2));
  c c_1 (
    .A(n4_bit_up_sync_counter_1_out_4), .B(n4_bit_up_sync_counter_1_out_3),
    .C(n4_bit_up_sync_counter_1_out_2), .D(n4_bit_up_sync_counter_1_out_1), .c_2(out_3));
  _7_Segment_Display u_7_segment_display_1 (
    .g(out_4), .f(out_5), .a(out_6), .b(out_7), .e(out_1), .d(out_2), .c(out_3));  // open: dp

  // Notes on the sheet:
  //   2107096
endmodule

module hexa_to_7seg_reverse (
  output out_1,
  output out_2,
  output out_3,
  output out_4,
  output out_5,
  output out_6,
  output out_7
);

  wire n4_bit_down_sync_counter_1_out_1, n4_bit_down_sync_counter_1_out_2, n4_bit_down_sync_counter_1_out_3,
       n4_bit_down_sync_counter_1_out_4;

  _4_bit_down_sync_counter u_4_bit_down_sync_counter_1 (
    .out_1(n4_bit_down_sync_counter_1_out_1), .out_2(n4_bit_down_sync_counter_1_out_2),
    .out_3(n4_bit_down_sync_counter_1_out_3), .out_4(n4_bit_down_sync_counter_1_out_4));
  b b_1 (
    .A(n4_bit_down_sync_counter_1_out_1), .B(n4_bit_down_sync_counter_1_out_2),
    .C(n4_bit_down_sync_counter_1_out_3), .D(n4_bit_down_sync_counter_1_out_4), .b_2(out_7));
  a a_1 (
    .A(n4_bit_down_sync_counter_1_out_1), .B(n4_bit_down_sync_counter_1_out_2),
    .C(n4_bit_down_sync_counter_1_out_3), .D(n4_bit_down_sync_counter_1_out_4), .a_2(out_6));
  f f_1 (
    .A(n4_bit_down_sync_counter_1_out_1), .B(n4_bit_down_sync_counter_1_out_2),
    .C(n4_bit_down_sync_counter_1_out_3), .D(n4_bit_down_sync_counter_1_out_4), .f(out_5));
  g g_1 (
    .A(n4_bit_down_sync_counter_1_out_1), .B(n4_bit_down_sync_counter_1_out_2),
    .C(n4_bit_down_sync_counter_1_out_3), .D(n4_bit_down_sync_counter_1_out_4), .g(out_4));
  e e_1 (
    .A(n4_bit_down_sync_counter_1_out_1), .B(n4_bit_down_sync_counter_1_out_2),
    .C(n4_bit_down_sync_counter_1_out_3), .D(n4_bit_down_sync_counter_1_out_4), .e(out_1));
  d d_1 (
    .A(n4_bit_down_sync_counter_1_out_1), .B(n4_bit_down_sync_counter_1_out_2),
    .C(n4_bit_down_sync_counter_1_out_3), .D(n4_bit_down_sync_counter_1_out_4), .d_2(out_2));
  c c_1 (
    .A(n4_bit_down_sync_counter_1_out_1), .B(n4_bit_down_sync_counter_1_out_2),
    .C(n4_bit_down_sync_counter_1_out_3), .D(n4_bit_down_sync_counter_1_out_4), .c_2(out_3));
  _7_Segment_Display u_7_segment_display_1 (
    .g(out_4), .f(out_5), .a(out_6), .b(out_7), .e(out_1), .d(out_2), .c(out_3));  // open: dp

  // Notes on the sheet:
  //   2107096
endmodule
